// Logisim project Erik2.circ as structural Verilog: 4 circuits, main circuit halfadder
module halfadder (
  input  a,
  input  b,
  output Sum,
  output Cout
);

  xor xor_1 (Sum, a, b);
  and and_1 (Cout, a, b);
endmodule

module FullAdder (
  input  Cin,
  input  A,
  input  B,
  output Sum,
  output Cout
);

  wire halfadder_1_cout, halfadder_1_sum, halfadder_2_cout;

  halfadder halfadder_1 (.a(A), .b(B), .Sum(halfadder_1_sum), .Cout(halfadder_1_cout));
  halfadder halfadder_2 (.a(Cin), .b(halfadder_1_sum), .Sum(Sum), .Cout(halfadder_2_cout));
  or or_1 (Cout, halfadder_2_cout, halfadder_1_cout);
endmodule

module Somador_de_2_Bits (
  input  A1,
  input  A0,
  input  B1,
  input  B0,
  input  Cin,
  output Sum,
  output Sum2,
  output Cout
);

  wire and_1_out, and_2_out, and_3_out, and_4_out, and_5_out, and_6_out, or_1_out;

  and and_1 (and_1_out, A0, B0);
  and and_2 (and_2_out, A0, Cin);
  and and_3 (and_3_out, B0, Cin);
  and and_4 (and_4_out, A1, B1);
  and and_5 (and_5_out, A1, or_1_out);
  and and_6 (and_6_out, B1, or_1_out);
  or or_1 (or_1_out, and_1_out, and_2_out, and_3_out);
  xor xor_1 (Sum, A0, B0, Cin);
  or or_2 (Cout, and_4_out, and_5_out, and_6_out);
  xor xor_2 (Sum2, A1, B1, or_1_out);
endmodule

module Somador_de_4_Bits (
  input  A3,
  input  A2,
  input  A1,
  input  A0,
  input  B3,
  input  B2,
  input  B1,
  input  B0,
  input  CIN,
  output Sum0,
  output Sum1,
  output Sum2,
  output Sum3,
  output Cout
);

  wire fulladder_1_cout, fulladder_2_cout, fulladder_3_cout;

  FullAdder fulladder_1 (.Cin(CIN), .A(A0), .B(B0), .Sum(Sum0), .Cout(fulladder_1_cout));
  FullAdder fulladder_2 (.Cin(fulladder_1_cout), .A(A1), .B(B1), .Sum(Sum1), .Cout(fulladder_2_cout));
  FullAdder fulladder_3 (.Cin(fulladder_2_cout), .A(B2), .B(A2), .Sum(Sum2), .Cout(fulladder_3_cout));
  FullAdder fulladder_4 (.Cin(fulladder_3_cout), .A(A3), .B(B3), .Sum(Sum3), .Cout(Cout));
endmodule
